# Fritzing sketch Wiring (saved by Fritzing 0.9.3b)
breadboards: 1

parts:
  Part1 = Arduino Uno (Rev3)
  J1 = Basic Servo
  J2 = Basic Servo
  LED1 = LED - 5mm [color="Red (633nm)" package="5 mm [THT]"]
  R1 = Resistor [tolerance=±5% resistance=220 package=THT]  # not connected
  IR1 = TSOP312.., 314.. [package=THT]
  Power_plug1 = Power plug
  U1 = Mini-360 DC-DC Buck converter [package=THT]
  Power_plug2 = Power plug  # not connected

nets:
  N1: Part1.D9_PWM, J2.pulse
  N2: Part1.D11_PWM/MOSI, J1.pulse
  N3: Part1.D3_PWM, IR1.Data
  N4: Part1.5V, IR1.Vs
  GND: Part1.GND, J1.gnd, J2.gnd, LED1.cathode, IR1.GND, U1.OUT-
  VCC: J1.vcc, J2.vcc, U1.OUT+
  N5: Power_plug1.GND, U1.IN+
  N6: Power_plug1.VCC, U1.IN-

notes:
  POWER IN
  FOR THE ARDUINO
  5V @250mA
  COMMON GROUND
  POWER FOR THE SERVO'S
  12V @2.3A
  DC STEP DOWN CONVERTER TO 9V
  IR SENSOR

custom parts:
  Mini-360 DC-DC Buck converter: Mini-360 DC-DC Buck converter. Tiny buck step down voltage converter, input voltage 4.75 to 23V output 1 to 17V adjustable. Available from ebay and the like.

// code stored in the sketch: Automatische Gordijnen.ino

